// Logisim project lab2_prob1.circ as structural Verilog: 1 circuit, main circuit main
module main (
  input  a,
  input  b,
  input  c,
  input  a_2,
  input  b_2,
  input  c_2,
  output F,
  output G
);

  wire _1_2_out, _1_out, _2_2_out, _2_out, _3_2_out, _3_out, _4_out, _5_out, and_1_out, and_2_out, and_3_out,
       and_4_out, and_5_out, not_1_out, not_2_out, not_3_out;

  not not_1 (not_1_out, a_2);
  not not_2 (not_2_out, b_2);
  not not_3 (not_3_out, b_2);
  and _1 (_1_out, a, b);
  and and_1 (and_1_out, a, b);
  and _1_2 (_1_2_out, not_1_out, not_2_out);
  and and_2 (and_2_out, a_2, not_3_out);
  and and_3 (and_3_out, b_2, a_2);
  and _2 (_2_out, _1_out, c);
  and _2_2 (_2_2_out, _1_2_out, c_2);
  and and_4 (and_4_out, and_2_out, c_2);
  and and_5 (and_5_out, and_3_out, c_2);
  or _3 (_3_out, _2_out, and_1_out);
  or _3_2 (_3_2_out, _2_2_out, and_4_out);
  or _4 (_4_out, _3_out, c);
  or _4_2 (G, _3_2_out, and_5_out);
  or _5 (_5_out, _4_out, b);
  or _6 (F, _5_out, a);

  // Notes on the sheet:
  //   F = abc + ab + a + b + c
  //   ** numbers indicate longest path
  //   G = a'b'c + ab'c + abc
  //   ** numbers indicate longest path
endmodule
