// Logisim project lab2_prob2.circ as structural Verilog: 1 circuit, main circuit main
module main (
  input  _0,
  input  _1,
  input  _2,
  input  _3,
  input  _4,
  input  _5,
  input  _6,
  output _2_2,
  output _2_1,
  output _2_0,
  output out_11,
  output out_12,
  output out_13,
  output out_14,
  output out_15,
  output out_16,
  output out_17
);

  wire _0_out, _1_out, _2_out, _3_out, _4_out, _5_out, _6_out, not_1_out, not_2_out, not_3_out;

  or or_1 (_2_2, _4, _5, _6);
  or or_2 (_2_1, _2, _3, _6);
  or or_3 (_2_0, _1, _3, _5);
  not not_1 (not_1_out, _2_0);
  not not_2 (not_2_out, _2_1);
  not not_3 (not_3_out, _2_2);
  _7_Segment_Display u_7_segment_display_1 (
    .g(out_17), .f(out_16), .a(out_11), .b(out_12), .e(out_15), .d(out_14), .c(out_13));  // open: dp
  and u__0 (_0_out, not_3_out, not_2_out, not_1_out);
  and u__1 (_1_out, not_3_out, not_2_out, _2_0);
  and u__2 (_2_out, not_3_out, _2_1, not_1_out);
  and u__3 (_3_out, not_3_out, _2_1, _2_0);
  and u__4 (_4_out, _2_2, not_2_out, not_1_out);
  and u__5 (_5_out, _2_2, not_2_out, _2_0);
  and u__6 (_6_out, _2_2, _2_1, not_1_out);
  or B (out_12, _0_out, _1_out, _2_out, _3_out, _4_out);
  or A (out_11, _0_out, _2_out, _3_out, _5_out, _6_out);
  or C (out_13, _0_out, _1_out, _3_out, _4_out, _5_out, _6_out);
  or D (out_14, _0_out, _2_out, _3_out, _5_out, _6_out);
  or F (out_16, _0_out, _4_out, _5_out, _6_out);
  or E (out_15, _0_out, _2_out, _6_out);
  or G (out_17, _2_out, _3_out, _4_out, _5_out, _6_out);

  // Notes on the sheet:
  //   ENCODER
  //   BUS
  //   DECODER
endmodule
